# Fritzing sketch light_dance (saved by Fritzing 0.9.4)
breadboards: 1

parts:
  Part1 = Arduino Uno (Rev3)
  LED1 = smd LED [color="Red (633nm)" package="0805 [SMD]"]
  LED2 = LED - 5mm [color="Red (633nm)" package="5 mm [THT]"]
  LED3 = smd LED [color="Red (633nm)" package="0805 [SMD]"]
  LED4 = smd LED [color="Red (633nm)" package="0805 [SMD]"]
  LED5 = smd LED [color="Red (633nm)" package="0805 [SMD]"]
  LED6 = smd LED [color="Red (633nm)" package="0805 [SMD]"]
  LED7 = smd LED [color="Red (633nm)" package="0805 [SMD]"]
  LED8 = smd LED [color="Red (633nm)" package="0805 [SMD]"]
  R1 = Resistor [tolerance=±5% resistance=220 package="1206 [SMD]"]
  R2 = Resistor [tolerance=±5% resistance=220 package="1206 [SMD]"]
  R3 = Resistor [tolerance=±5% resistance=220 package="1206 [SMD]"]
  R4 = Resistor [tolerance=±5% resistance=220 package="1206 [SMD]"]
  R5 = Resistor [tolerance=±5% resistance=220 package="1206 [SMD]"]
  R6 = Resistor [tolerance=±5% resistance=220 package="1206 [SMD]"]
  R7 = Resistor [tolerance=±5% resistance=220 package="1206 [SMD]"]
  R8 = Resistor [tolerance=±5% resistance=220 package="1206 [SMD]"]
  S1 = Pushbutton [package="[SMD]"]
  S2 = Pushbutton [package="[SMD]"]
  S3 = Pushbutton [package="[SMD]"]
  R9 = Resistor [tolerance=±5% resistance=220 package="2512 [SMD]"]
  R10 = Resistor [tolerance=±5% resistance=220 package="2512 [SMD]"]
  R11 = Resistor [tolerance=±5% resistance=220 package="2512 [SMD]"]

nets:
  N1: Part1.A0, S3.Pin_1, S3.Pin_2, R10.Pin_0
  N2: Part1.A1, S2.Pin_1, S2.Pin_2, R9.Pin_0
  N3: Part1.A2, S1.Pin_1, S1.Pin_2, R11.Pin_0
  N4: Part1.GND, R1.Pin_0, R2.Pin_0, R3.Pin_0, R4.Pin_0, R5.Pin_0, R6.Pin_0, R7.Pin_0, R8.Pin_0, S1.Pin_3, S1.Pin_4, S2.Pin_3, S2.Pin_4, S3.Pin_3, S3.Pin_4
  N5: Part1.D0/RX, LED7.anode
  N6: Part1.D1/TX, LED1.anode
  N7: Part1.D2, LED8.anode
  N8: Part1.D3_PWM, LED2.anode
  N9: Part1.D4, LED3.anode
  N10: Part1.D5_PWM, LED4.anode
  N11: Part1.D6_PWM, LED5.anode
  N12: Part1.D7, LED6.anode
  N13: Part1.5V, R9.Pin_1, R10.Pin_1, R11.Pin_1
  N14: LED1.cathode, R8.Pin_1
  N15: LED2.cathode, R6.Pin_1
  N16: LED3.cathode, R5.Pin_1
  N17: LED4.cathode, R4.Pin_1
  N18: LED5.cathode, R3.Pin_1
  N19: LED6.cathode, R2.Pin_1
  N20: LED7.cathode, R1.Pin_1
  N21: LED8.cathode, R7.Pin_1
